# Fritzing sketch Turing-Robot_Sketch (saved by Fritzing 0.9.3b)

parts:
  Rueda_DI = DC Motor  # not connected
  Rueda_TI = DC Motor  # not connected
  S1 = Taiway 100-SP-X-T1 SPDT Miniature Toggle Switch [part_number=100-SP-X-T1-0-0-B1-M1 package=THT]
  Rueda_TD = DC Motor  # not connected
  Rueda_DD = DC Motor  # not connected
  L1 = Solenoid  # not connected
  U1 = LIPO-1000mAh [package=lipo-1000]

nets:
  N1: S1.L2, U1.+

notes:
  M1
  M2
  M5
